// Logisim project cronometro.circ as structural Verilog: 10 circuits, main circuit main
module main (
  input  [1:0] VEL_SEL,
  input  START,
  input  RESET,
  input  [8:0] in_4
);

  wire CLK_out, finish_comparator_1_fin, not_1_out, or_1_out, state_machine_1_enable_count,
       state_machine_1_finish_led, tick_generator_1_tick_out;
  wire [3:0] binary_to_bcd_converter_1_p2, binary_to_bcd_converter_1_p3, binary_to_bcd_converter_1_p4,
       display_block_1_min_dec, display_block_1_min_uni, display_block_1_seg_dec, display_block_1_seg_uni,
       speed_selector_1_decimal_bcd, speed_selector_1_speed_bcd;
  wire [8:0] binary_to_bcd_converter_1_p1;

  TICK_GENERATOR tick_generator_1 (.VEL_SEL(VEL_SEL), .TICK_OUT(tick_generator_1_tick_out));
  Clock CLK (.out(CLK_out));
  SPEED_SELECTOR speed_selector_1 (
    .VEL_SEL(VEL_SEL), .SPEED_BCD(speed_selector_1_speed_bcd), .DECIMAL_BCD(speed_selector_1_decimal_bcd));
  Hex_Digit_Display hex_digit_display_1 (.value(speed_selector_1_speed_bcd));  // open: dp
  Hex_Digit_Display hex_digit_display_2 (.value(speed_selector_1_decimal_bcd));  // open: dp
  STATE_MACHINE state_machine_1 (
    .START(START), .FIN(finish_comparator_1_fin), .RESET(RESET), .CLK(CLK_out),
    .ENABLE_COUNT(state_machine_1_enable_count), .FINISH_LED(state_machine_1_finish_led));
  not not_1 (not_1_out, state_machine_1_enable_count);
  or or_1 (or_1_out, not_1_out, RESET);
  LED FIN (.in(state_machine_1_finish_led));
  Hex_Digit_Display hex_digit_display_3 (.value(display_block_1_min_dec));  // open: dp
  Hex_Digit_Display hex_digit_display_4 (.value(binary_to_bcd_converter_1_p2));  // open: dp
  // Binary_to_BCD_converter binary_to_bcd_converter_1: pin names not known; wires that end beside it: binary_to_bcd_converter_1_p1, binary_to_bcd_converter_1_p2, binary_to_bcd_converter_1_p3, binary_to_bcd_converter_1_p4
  FINISH_COMPARATOR finish_comparator_1 (
    .TIEMPO_ACTUAL(binary_to_bcd_converter_1_p1), .TIEMPO_CONFIG(in_4), .FIN(finish_comparator_1_fin));
  Hex_Digit_Display hex_digit_display_5 (.value(display_block_1_min_uni));  // open: dp
  Hex_Digit_Display hex_digit_display_6 (.value(display_block_1_seg_dec));  // open: dp
  Hex_Digit_Display hex_digit_display_7 (.value(binary_to_bcd_converter_1_p3));  // open: dp
  Hex_Digit_Display hex_digit_display_8 (.value(display_block_1_seg_uni));  // open: dp
  Hex_Digit_Display hex_digit_display_9 (.value(binary_to_bcd_converter_1_p4));  // open: dp
  CHRONOMETER chronometer_1 (
    .TICK_IN(tick_generator_1_tick_out), .RESET(or_1_out), .TIEMPO_ACTUAL(binary_to_bcd_converter_1_p1));
  DISPLAY_BLOCK display_block_1 (
    .TIEMPO_ACTUAL(binary_to_bcd_converter_1_p1), .MIN_DEC(display_block_1_min_dec),
    .MIN_UNI(display_block_1_min_uni), .SEG_DEC(display_block_1_seg_dec), .SEG_UNI(display_block_1_seg_uni));

  // Notes on the sheet:
  //   Tiempo
  //   :
endmodule

// reloj
module TICK_GENERATOR (
  input  [1:0] VEL_SEL,
  output TICK_OUT
);

  wire A_out, B_out, C_out;

  Clock #(.highDuration(2), .lowDuration(2)) A (.out(A_out));
  Clock #(.lowDuration(2)) B (.out(B_out));
  Clock C (.out(C_out));
  Multiplexer #(.select(2)) multiplexer_1 (
    .in0(A_out), .in1(B_out), .in2(C_out), .in3(1'b0), .out(TICK_OUT), .sel(VEL_SEL));
endmodule

module CHRONOMETER (
  input  TICK_IN,
  input  RESET,
  output [8:0] TIEMPO_ACTUAL
);

  Counter #(.max('h1ff), .ongoal("stay"), .width(9)) counter_1 (
    .load(1'b0), .D({9{1'b0}}), .count(1'b1), .Q(TIEMPO_ACTUAL), .up(1'b1), .clk(TICK_IN), .clr(RESET));  // open: carry
endmodule

module FINISH_COMPARATOR (
  input  [8:0] TIEMPO_ACTUAL,
  input  [8:0] TIEMPO_CONFIG,
  output FIN
);

  wire comparator_1_gt, comparator_1_lt;

  Comparator #(.width(9)) comparator_1 (
    .a(TIEMPO_ACTUAL), .b(TIEMPO_CONFIG), .gt(comparator_1_gt), .eq(FIN), .lt(comparator_1_lt));
  // NoConnect on comparator_1_gt
  // NoConnect on comparator_1_lt
endmodule

module DISPLAY_BLOCK (
  input  [8:0] TIEMPO_ACTUAL,
  output [3:0] MIN_DEC,
  output [3:0] MIN_UNI,
  output [3:0] SEG_DEC,
  output [3:0] SEG_UNI
);

  wire [8:0] divider_1_out, divider_1_rem;
  wire [8:4] divider_2_out, divider_2_rem, divider_3_out, divider_3_rem;

  Divider #(.width(9)) divider_1 (
    .a(TIEMPO_ACTUAL), .b(9'h3c), .out(divider_1_out), .rem(divider_1_rem));  // open: upper
  Divider #(.width(9)) divider_2 (
    .a(divider_1_out), .b(9'ha), .out({divider_2_out, MIN_DEC}), .upper({9{1'b0}}),
    .rem({divider_2_rem, MIN_UNI}));
  Divider #(.width(9)) divider_3 (
    .a(divider_1_rem), .b(9'ha), .out({divider_3_out, SEG_DEC}), .rem({divider_3_rem, SEG_UNI}));  // open: upper
  // also tied to GND on the sheet: {divider_2_out[4], divider_2_out[5], divider_2_out[6], divider_2_out[7], divider_2_out[8], divider_2_rem[4], divider_2_rem[5], divider_2_rem[6], divider_2_rem[7], divider_2_rem[8], divider_3_out[4], divider_3_out[5], divider_3_out[6], divider_3_out[7], divider_3_out[8], divider_3_rem[4], divider_3_rem[5], divider_3_rem[6], divider_3_rem[7], divider_3_rem[8]}
endmodule

module PULSE_DETECTOR (
  input  TICK_OUT,
  input  CLK,
  output PULSE
);

  wire FF1_q, FF2_q, not_1_out;

  D_Flip_Flop FF1 (.D(TICK_OUT), .clk(CLK), .Q(FF1_q), .preset(1'b0), .reset(1'b0));  // open: Qn
  D_Flip_Flop FF2 (.D(FF1_q), .clk(CLK), .Q(FF2_q), .preset(1'b0), .reset(1'b0));  // open: Qn
  not not_1 (not_1_out, FF2_q);
  and and_1 (PULSE, FF1_q, not_1_out);
endmodule

module STATE_MACHINE (
  input  START,
  input  FIN,
  input  RESET,
  input  CLK,
  output ENABLE_COUNT,
  output FINISH_LED
);

  wire and_1_out, and_2_out, and_3_out, and_6_out, NEXT0_out, NEXT1_out, not_1_out, not_2_out, not_3_out,
       not_4_out, not_5_out, not_6_out, not_7_out, not_8_out, not_9_out, not_10_out, not_11_out, not_12_out,
       STATE0, STATE1;

  not not_1 (not_1_out, STATE0);
  not not_2 (not_2_out, STATE1);
  D_Flip_Flop FF1 (.D(NEXT1_out), .clk(CLK), .Q(STATE1), .preset(1'b0), .reset(1'b0));  // open: Qn
  or NEXT0 (NEXT0_out, and_1_out, and_2_out);
  and and_1 (and_1_out, not_2_out, not_1_out, START, not_3_out);
  not not_3 (not_3_out, RESET);
  not not_4 (not_4_out, STATE1);
  D_Flip_Flop FF0 (.D(NEXT0_out), .clk(CLK), .Q(STATE0), .preset(1'b0), .reset(1'b0));  // open: Qn
  and and_2 (and_2_out, not_4_out, STATE0, not_5_out, not_6_out);
  not not_5 (not_5_out, FIN);
  not not_6 (not_6_out, RESET);
  and and_3 (and_3_out, not_7_out, STATE0, FIN, not_8_out);
  not not_7 (not_7_out, STATE1);
  not not_8 (not_8_out, RESET);
  not not_9 (not_9_out, STATE1);
  not not_10 (not_10_out, STATE0);
  or NEXT1 (NEXT1_out, and_3_out, and_6_out);
  and and_4 (ENABLE_COUNT, not_9_out, STATE0);
  and and_5 (FINISH_LED, STATE1, not_10_out);
  and and_6 (and_6_out, STATE1, not_11_out, not_12_out);
  not not_11 (not_11_out, STATE0);
  not not_12 (not_12_out, RESET);

  // Notes on the sheet:
  //   Ivan
endmodule

module CONFIG_TIME (
  input  [3:0] MIN_DEC,
  input  [3:0] MIN_UNI,
  input  [3:0] SEG_DEC,
  input  [3:0] SEG_UNI,
  output [11:0] TIEMPO_CONFIG,
  output [7:0] MINUTOS_TOTALES,
  output [11:0] MINUTOS_EN_SEGUNDOS,
  output [7:0] SEGUNDOS_TOTALES
);

  wire [7:0] bit_extender_1_out, bit_extender_2_out, bit_extender_3_out, bit_extender_4_out,
       multiplier_1_out, multiplier_2_out;
  wire [11:0] bit_extender_5_out, bit_extender_6_out;

  assign bit_extender_1_out = {{4{MIN_DEC[3]}}, MIN_DEC};  // Bit_Extender bit_extender_1
  assign bit_extender_2_out = {{4{1'b0}}, SEG_DEC};  // Bit_Extender bit_extender_2
  Multiplier multiplier_1 (.a(bit_extender_1_out), .b(8'ha), .out(multiplier_1_out));  // open: cin, cout
  Multiplier multiplier_2 (.a(bit_extender_2_out), .b(8'ha), .out(multiplier_2_out));  // open: cin, cout
  Adder adder_1 (.a(multiplier_1_out), .b(bit_extender_3_out), .out(MINUTOS_TOTALES));  // open: cin, cout
  assign bit_extender_3_out = {{4{1'b0}}, MIN_UNI};  // Bit_Extender bit_extender_3
  assign bit_extender_4_out = {{4{1'b0}}, SEG_UNI};  // Bit_Extender bit_extender_4
  Adder adder_2 (.a(multiplier_2_out), .b(bit_extender_4_out), .out(SEGUNDOS_TOTALES));  // open: cin, cout
  assign bit_extender_5_out = {{4{1'b0}}, MINUTOS_TOTALES};  // Bit_Extender bit_extender_5
  Multiplier #(.width(12)) multiplier_3 (
    .a(bit_extender_5_out), .b(12'h3c), .out(MINUTOS_EN_SEGUNDOS));  // open: cin, cout
  assign bit_extender_6_out = {{4{1'b0}}, SEGUNDOS_TOTALES};  // Bit_Extender bit_extender_6
  Adder #(.width(12)) adder_3 (
    .a(MINUTOS_EN_SEGUNDOS), .b(bit_extender_6_out), .out(TIEMPO_CONFIG));  // open: cin, cout

  // Notes on the sheet:
  //   0-5
  //   RANGO
  //   0-9
  //   0-5
  //   0--9
endmodule

module SPEED_SELECTOR (
  input  [1:0] VEL_SEL,
  output [3:0] SPEED_BCD,
  output [3:0] DECIMAL_BCD
);

  wire pulse_detector_1_pulse, tick_generator_1_tick_out;
  wire [1:0] multiplexer_1_out;

  Multiplexer #(.select(2), .width(2)) multiplexer_1 (
    .in0(2'b00), .in1(2'b01), .in2(2'b10), .in3(2'b00), .out(multiplexer_1_out), .sel(VEL_SEL));
  Multiplexer #(.select(2), .width(4)) multiplexer_2 (
    .in0(4'b0001), .in1(4'b0001), .in2(4'b0010), .in3(4'b0000), .out(SPEED_BCD), .sel(VEL_SEL));
  Multiplexer #(.select(2), .width(4)) multiplexer_3 (
    .in0(4'b0000), .in1(4'b0101), .in2(4'b0000), .in3(4'b0000), .out(DECIMAL_BCD), .sel(VEL_SEL));
  TICK_GENERATOR tick_generator_1 (.VEL_SEL(multiplexer_1_out), .TICK_OUT(tick_generator_1_tick_out));
  PULSE_DETECTOR pulse_detector_1 (.TICK_OUT(tick_generator_1_tick_out), .PULSE(pulse_detector_1_pulse));  // open: CLK
  CHRONOMETER chronometer_1 (.TICK_IN(pulse_detector_1_pulse));  // open: RESET, TIEMPO_ACTUAL

  // Notes on the sheet:
  //   hecho por Ivan
endmodule

module test (
  output [3:0] out_1,
  output [3:0] out_2,
  output [3:0] out_3,
  output [3:0] out_4
);

  wire [3:0] display_block_1_min_dec, display_block_1_min_uni, display_block_1_seg_dec,
       display_block_1_seg_uni;

  DISPLAY_BLOCK display_block_1 (
    .TIEMPO_ACTUAL(9'ha), .MIN_DEC(display_block_1_min_dec), .MIN_UNI(display_block_1_min_uni),
    .SEG_DEC(display_block_1_seg_dec), .SEG_UNI(display_block_1_seg_uni));
  Hex_Digit_Display hex_digit_display_1 (.value(display_block_1_min_dec));  // open: dp
  Hex_Digit_Display hex_digit_display_2 (.value(display_block_1_min_uni));  // open: dp
  Hex_Digit_Display hex_digit_display_3 (.value(display_block_1_seg_dec));  // open: dp
  Hex_Digit_Display hex_digit_display_4 (.value(display_block_1_seg_uni));  // open: dp
endmodule
